# Fritzing sketch Esquema_Eletrico (saved by Fritzing 0.9.3b)
breadboards: 1

parts:
  HC-05 = Bluetooth HC-05 Macho
  Relay_4_ports = Module 4 Relais 5V [package="Module 4 Relais 5V"]
  WATER_PUMP1 = water pump/motor
  WATER_PUMP2 = water pump/motor
  WATER_PUMP3 = water pump/motor
  WATER_PUMP4 = water pump/motor
  Arduino_UNO = Arduino Uno (Rev3)
  BAT1 = 12 battery [package=battery]

nets:
  N1: HC-05.TXD, Arduino_UNO.D12/MISO
  N2: HC-05.RXD, Arduino_UNO.D13/SCK
  VCC: HC-05.VCC, Relay_4_ports.VCC, Arduino_UNO.5V
  GND: HC-05.GND, Relay_4_ports.GND, Arduino_UNO.GND
  N3: Relay_4_ports.IN1, Arduino_UNO.D2
  N4: Relay_4_ports.IN2, Arduino_UNO.D3_PWM
  N5: Relay_4_ports.IN3, Arduino_UNO.D4
  N6: Relay_4_ports.IN4, Arduino_UNO.D5_PWM
  N7: Relay_4_ports.K1-NF, Relay_4_ports.K2-NF, Relay_4_ports.K3-NF, Relay_4_ports.K4-NF, BAT1.-
  N8: Relay_4_ports.K1-NO, WATER_PUMP1.pin_2
  N9: Relay_4_ports.K2-NO, WATER_PUMP2.pin_2
  N10: Relay_4_ports.K3-NO, WATER_PUMP3.pin_2
  N11: Relay_4_ports.K4-NO, WATER_PUMP4.pin_2
  N12: WATER_PUMP1.pin_1, WATER_PUMP2.pin_1, WATER_PUMP3.pin_1, WATER_PUMP4.pin_1, BAT1.+

custom parts:
  Module 4 Relais 5V: Module 4 Relais 5V 4x SPD-06VDC-SD-C
  water pump/motor: WATER PUMP BY ARDUBLOCKTR
  12 battery: 12V lead acid type battery, like the Husqvarna YTH2448 12V 35AH battery. The pads in pcb are sized to accomidate up to 14ga wire (as these batterys will deliver high currents.)
